# Fritzing sketch Circuit (saved by Fritzing 0.9.5d)
breadboards: 1

parts:
  Raspberry_Pi_1 = Raspberry Pi 3 [part_number=RPI-3-V1.2]
  U1 = 4-Channel 5v Relay Shield [package=relay-4ch5v10a]
  J1 = 2.1mm Barrel Jack with Terminal Block
  LED1 = LEDs [package=led10mm]

nets:
  3V3: Raspberry_Pi_1.3v3, Raspberry_Pi_1.3V3
  GND: Raspberry_Pi_1.GND, U1.GND
  N1: Raspberry_Pi_1.GIPO5, U1.IN1
  N2: Raspberry_Pi_1.GIPO6, U1.IN2
  N3: Raspberry_Pi_1.GIPO13, U1.IN3
  N4: Raspberry_Pi_1.GIPO19, U1.IN4
  5V: Raspberry_Pi_1.5V, U1.VCC
  N5: U1.K1-In, U1.K2-In, J1.POS
  N6: U1.K4-Off, LED1.A

notes:
  Only Connect Blue wires if the fans are not rotating. If they are rotating, skip blue wires connections
  220v AC

custom parts:
  4-Channel 5v Relay Shield: 4 Channel 5v Relay Shield w. 2x SPD-06VDC-SD-C
  LEDs: LEDs Standard schematic elements and footprints for 5mm, 3mm, 1206, and 0603 sized LEDs. 5mm - Spark Fun Electronics SKU : COM-00529 (and others)
